// Logisim project AluBebe.circ as structural Verilog: 3 circuits, main circuit Alu
module Alu (
  input  [7:0] N,
  input  [7:0] R0,
  input  [7:0] R1,
  input  [3:0] Banderas,
  input  [4:0] Instrucciones,
  output [7:0] ACC,
  output [7:0] ACC2,
  output [3:0] BanderasOut
);

  wire [19:0] add_1_salida;

  add add_1 (.Entrada({Banderas, R1, R0, N}), .Salida(add_1_salida));
  Multiplexer #(.select(5), .width(20)) multiplexer_1 (
    .in0(add_1_salida), .out({BanderasOut, ACC2, ACC}), .sel(Instrucciones));  // open: in1, in2, in3, in4, in5, in6, in7, in8, in9, in10, in11, in12, in13, in14, in15, in16, in17, in18, in19, in20, in21, in22, in23, in24, in25, in26, in27, in28, in29, in30, in31
endmodule

module add (
  input  [27:0] Entrada,
  output [19:0] Salida
);

  Adder adder_1 (.a(Entrada[7:0]), .b(Entrada[15:8]), .out(Salida[7:0]), .cin(Entrada[27]));  // open: cout

  assign Salida[19:8] = Entrada[27:16];
  // also tied to GND on the sheet: Entrada[27]

  // Notes on the sheet:
  //   N
  //   R0
  //   R1
endmodule

module xchg (
  input  [27:0] Entrada
);
endmodule
